# Fritzing sketch KnopLedBoard (saved by Fritzing 0.9.3b)
circuit board: 8.46667cm x 5.64444cm
stripboards: 1

parts:
  Input = Led and switch connector [package=THT]
  Output = Led and switch connector [package=THT]
  Led0/1 = female pin header, 2 pins [form="♀ (female)"]
  Led2/3 = female pin header, 2 pins [form="♀ (female)"]
  Led4/5 = female pin header, 2 pins [form="♀ (female)"]
  U1 = 74HC595 [package="DIP16 [THT]"]
  Switches = female pin header, 2 pins [form="♀ (female)"]
  R1 = Resistor [tolerance=±5% resistance=100k package=THT]

nets:
  N1: Input.DS, U1.DS
  GND: Input.Gnd, Output.Gnd, U1.GND, U1.OE, Switches.pin1
  N2: Input.ST_CP, Output.ST_CP, U1.ST_CP
  N3: Input.SH_CP, Output.SH_CP, U1.SH_CP
  VCC: Input.Vcc, Output.Vcc, U1.MR, U1.VCC, R1.Pin_1
  N4: Output.DS, U1.Q7'
  N5: Led0/1.pin1, U1.Q1
  N6: Led0/1.pin2, U1.Q2
  N7: Led2/3.pin1, U1.Q3
  N8: Led2/3.pin2, U1.Q4
  N9: Led4/5.pin1, U1.Q5
  N10: Led4/5.pin2, U1.Q6
  N11: Switches.pin2, R1.Pin_0
