# Fritzing sketch KnopLedBoardDubbel (saved by Fritzing 0.9.3b)
circuit board: 8.46667cm x 5.64444cm
stripboards: 1

parts:
  U2 = 74HC595 [package="DIP16 [THT]"]
  R1 = Resistor [tolerance=±5% resistance=100k package=THT]
  Output = Led and switch connector [package=THT]
  Led4/5 = female pin header, 2 pins [form="♀ (female)"]
  Input = Led and switch connector [package=THT]
  R2 = Resistor [tolerance=±5% resistance=100k package=THT]
  Led0/1 = female pin header, 2 pins [form="♀ (female)"]
  U1 = 74HC595 [package="DIP16 [THT]"]
  Led2/3 = female pin header, 2 pins [form="♀ (female)"]

nets:
  GND: U2.GND, U2.OE, Output.Gnd, Input.Gnd, U1.GND, U1.OE
  N1: U2.Q7', Output.DS
  VCC: U2.MR, U2.VCC, R1.Pin_1, Output.Vcc, Input.Vcc, R2.Pin_1, U1.MR, U1.VCC
  N2: U2.SH_CP, Output.SH_CP, Input.SH_CP, U1.SH_CP
  N3: U2.ST_CP, Output.ST_CP, Input.ST_CP, U1.ST_CP
  N4: U2.DS, U1.Q7'
  N5: Led4/5.pin1, U1.Q5
  N6: Led4/5.pin2, U1.Q6
  N7: Input.DS, U1.DS
  N8: Led0/1.pin1, U1.Q1
  N9: Led0/1.pin2, U1.Q2
  N10: U1.Q3, Led2/3.pin1
  N11: U1.Q4, Led2/3.pin2
