# Fritzing sketch Small switch (saved by Fritzing 0.9.3b)
breadboards: 1

parts:
  Part1 = Arduino Uno (Rev3)
  U1 = 74HC595 [package="DIP16 [THT]"]
  S2 = Pushbutton [package="[THT]"]
  S3 = Pushbutton [package="[THT]"]
  S4 = Pushbutton [package="[THT]"]
  S5 = Pushbutton [package="[THT]"]
  S1 = Pushbutton [package="[THT]"]
  R1 = Resistor [tolerance=±5% resistance=10k package=THT]
  R2 = Resistor [tolerance=±5% resistance=10k package=THT]
  R3 = Resistor [tolerance=±5% resistance=10k package=THT]
  R4 = Resistor [tolerance=±5% resistance=10k package=THT]
  R5 = Resistor [tolerance=±5% resistance=10k package=THT]
  R6 = Resistor [tolerance=±5% resistance=100k package=THT]
  LED1 = LED - 5mm [color="Red (633nm)" package="5 mm [THT]"]
  LED2 = LED - 5mm [color="Red (633nm)" package="5 mm [THT]"]
  LED3 = LED - 5mm [color="Red (633nm)" package="5 mm [THT]"]
  LED4 = LED - 5mm [color="Red (633nm)" package="5 mm [THT]"]
  LED5 = LED - 5mm [color="Red (633nm)" package="5 mm [THT]"]
  R7 = Resistor [tolerance=±5% resistance=220 package=THT]

nets:
  N1: Part1.A0, S2.Pin_1, S2.Pin_2, S3.Pin_1, S3.Pin_2, S4.Pin_1, S4.Pin_2, S5.Pin_1, S5.Pin_2, S1.Pin_1, S1.Pin_2, R6.Pin_0
  GND: Part1.GND, U1.GND, U1.OE, R1.Pin_1, R7.Pin_1
  N2: Part1.D2, U1.SH_CP
  N3: Part1.D3_PWM, U1.ST_CP
  N4: Part1.D4, U1.DS
  5V: Part1.5V, U1.MR, U1.VCC, R6.Pin_1
  N5: U1.Q1, LED1.anode
  N6: U1.Q2, LED2.anode
  N7: U1.Q3, LED3.anode
  N8: U1.Q4, LED4.anode
  N9: U1.Q5, LED5.anode
  N10: S2.Pin_3, S2.Pin_4, R2.Pin_0, R3.Pin_1
  N11: S3.Pin_3, S3.Pin_4, R3.Pin_0, R4.Pin_1
  N12: S4.Pin_3, S4.Pin_4, R4.Pin_0, R5.Pin_1
  N13: S5.Pin_3, S5.Pin_4, R5.Pin_0
  N14: S1.Pin_3, S1.Pin_4, R1.Pin_0, R2.Pin_1
  N15: LED1.cathode, LED2.cathode, LED3.cathode, LED4.cathode, LED5.cathode, R7.Pin_0
